// Logisim project project1.circ as structural Verilog: 1 circuit, main circuit main
module main (
  input  A,
  input  B,
  input  C,
  input  D,
  output W,
  output X,
  output Y,
  output Z,
  output E
);

  wire and_1_out, and_2_out, and_4_out, and_5_out, and_6_out, and_7_out, not_1_out, not_2_out, not_3_out;

  not not_1 (not_1_out, A);
  not not_2 (not_2_out, B);
  not not_3 (not_3_out, C);
  and and_1 (and_1_out, A, B);
  and and_2 (and_2_out, A, C);
  and and_3 (X, A, not_2_out, not_3_out);
  and and_4 (and_4_out, not_1_out, B);
  and and_5 (and_5_out, B, not_2_out);
  and and_6 (and_6_out, A, B, not_3_out);
  and and_7 (and_7_out, not_1_out, C);
  or or_1 (W, and_1_out, and_2_out);
  or or_2 (Y, and_4_out, and_5_out);
  or or_3 (Z, and_6_out, and_7_out);

  assign E = D;
endmodule
